# Fritzing sketch flash_programmer (saved by Fritzing 0.9.3b)
breadboards: 1

parts:
  Part1 = Arduino Mega ADK (Rev3)
  IC2 = DIP - 32 pins [package="DIP (Dual Inline) [THT]"]
  IC3 = DIP - 32 pins [package="DIP (Dual Inline) [THT]"]

nets:
  N1: Part1.A8, IC2.pin27, IC3.pin27
  N2: Part1.A9, IC2.pin26, IC3.pin26
  N3: Part1.A10, IC2.pin23, IC3.pin23
  N4: Part1.A11, IC2.pin25, IC3.pin25
  N5: Part1.A12, IC2.pin4, IC3.pin4
  N6: Part1.A13, IC2.pin28, IC3.pin28
  N7: Part1.A14, IC2.pin29, IC3.pin29
  N8: Part1.A15, IC2.pin3, IC3.pin3
  N9: Part1.A0, IC2.pin12, IC3.pin12
  N10: Part1.A1, IC2.pin11, IC3.pin11
  N11: Part1.A2, IC2.pin10, IC3.pin10
  N12: Part1.A3, IC2.pin9, IC3.pin9
  N13: Part1.A4, IC2.pin8, IC3.pin8
  N14: Part1.A5, IC2.pin7, IC3.pin7
  N15: Part1.A6, IC2.pin6, IC3.pin6
  N16: Part1.A7, IC2.pin5, IC3.pin5
  N17: Part1.GND, IC2.pin16, IC3.pin16
  N18: Part1.5V, IC2.pin32, IC3.pin32
  N19: Part1.D22, IC3.pin13
  N20: Part1.D23, IC3.pin14
  N21: Part1.D24, IC3.pin15
  N22: Part1.D25, IC3.pin17
  N23: Part1.D26, IC3.pin18
  N24: Part1.D27, IC3.pin19
  N25: Part1.D28, IC3.pin20
  N26: Part1.D29, IC3.pin21
  N27: Part1.D30, IC2.pin21
  N28: Part1.D31, IC2.pin20
  N29: Part1.D32, IC2.pin19
  N30: Part1.D33, IC2.pin18
  N31: Part1.D34, IC2.pin17
  N32: Part1.D35, IC2.pin15
  N33: Part1.D36, IC2.pin14
  N34: Part1.D37, IC2.pin13
  N35: Part1.D44, IC2.pin31, IC3.pin31
  N36: Part1.D45, IC2.pin24, IC3.pin24
  N37: Part1.D46, IC2.pin22, IC3.pin22
  N38: Part1.D47, IC2.pin1, IC3.pin1
  N39: Part1.D48, IC2.pin30, IC3.pin30
  N40: Part1.D49, IC2.pin_2, IC3.pin_2

custom parts:
  DIP - 32 pins: SST39SF040 4 Mbit (x8) CMOS Multi-Purpose Flash.
